# Fritzing sketch led-test-bench (saved by Fritzing 0.9.3b)
circuit board: 8.46667cm x 5.64444cm
breadboards: 1

parts:
  RE1 = Rotary Encoder [package=THT]
  RE2 = Rotary Encoder [package=THT]
  S1 = Pushbutton [package="[THT]"]
  J1 = Screw terminal - 2 pins [package=THT]
  J2 = Screw terminal - 2 pins [package=THT]
  J3 = Screw terminal - 2 pins [package=THT]
  Part1 = Arduino Uno (Rev3)
  J4 = Power Jack [package=power_jack_combo]

nets (from the breadboard view):
  N1: RE1.EncoderPinA, RE2.EncoderPinA, S1.Pin_1, S1.Pin_2, J1.pin1, J2.pin1, Part1.VIN, J4.GNDBREAK
  N2: RE1.EncoderPinC, Part1.D9_PWM
  GND: RE1.EncoderPinB, RE2.EncoderPinB, J1.pin2, J2.pin2, Part1.GND, J4.GND
  N3: RE2.EncoderPinC, Part1.D8
  N4: S1.Pin_3, S1.Pin_4, Part1.D10_PWM/SS
  N5: J3.pin1, Part1.D6_PWM
  N6: J3.pin2, Part1.D7
